# Fritzing sketch DwarfmasterConnections (saved by Fritzing 0.9.9b)
breadboards: 1

parts:
  Teensy1 = Teensy 4.1
  LCD1 = elegoo-2.8in-tft-display
  S2 = Round Pushbutton
  S3 = Round Pushbutton
  S4 = Round Pushbutton
  S5 = Round Pushbutton
  S6 = Round Pushbutton
  S7 = Round Pushbutton
  TRS2 = Audio Jack (TRS) 3.5mm [package="PG203J [THT]"]
  R1 = Resistor [tolerance=±5% resistance=100 package="2512 [SMD]"]

nets:
  N1: Teensy1.GND, Teensy1.GND2#55, S2.leg1, S3.leg1, S4.leg1, S5.leg1, S6.leg1, S7.leg1, TRS2.Sleeve
  N2: Teensy1.D2, LCD1.LCD_D2
  N3: Teensy1.D3, LCD1.LCD_D3
  N4: Teensy1.D4, LCD1.LCD_D4
  N5: Teensy1.D5, LCD1.LCD_D5
  N6: Teensy1.D6, LCD1.LCD_D6
  N7: Teensy1.D7, LCD1.LCD_D7
  N8: Teensy1.D8, LCD1.LCD_D0
  N9: Teensy1.D9, LCD1.LCD_D1
  N10: Teensy1.A0/D14, LCD1.LCD_RD
  N11: Teensy1.A1/D15, LCD1.LCD_WR
  N12: Teensy1.A2/D16, LCD1.LCD_RS
  N13: Teensy1.A3/D17, LCD1.LCD_CS
  N14: Teensy1.A4/D18, LCD1.LCD_RST
  N15: Teensy1.A5/D19, TRS2.Ring
  N16: Teensy1.3V3_LOW, R1.Pin_1
  N17: Teensy1.GND2#31, LCD1.GND
  VIN: Teensy1.Vin, LCD1.5V
  N18: Teensy1.D33, S2.leg0
  N19: Teensy1.D34, S3.leg0
  N20: Teensy1.D35, S4.leg0
  N21: Teensy1.D36, S5.leg0
  N22: Teensy1.D37, S6.leg0
  N23: Teensy1.A14/D38, S7.leg0

notes:
  Button#1 -> D33
  Button#2 -> D34
  Button#3 -> D35
  Button#4 -> D36
  Button#5 -> D37
  Button#6 -> D38
  EXP -> D19
  The TIP is connected to D19 and the RING to 3.3V (Roland/Boss standard).
  The resistor is there to prevent shortcircuits when the jack is inserted or removed.
  LCD D0 -> D8
  LCD D1 -> D9
  LCD D2 -> D2
  LCD D3 -> D3
  LCD D4 -> D4
  LCD D5 -> D5
  LCD D6 -> D6
  LCD D7 -> D7
  LCD RD -> D14
  LCD WR -> D15
  LCD RS -> D16
  LCD CS - > D17
  LCD RST -> D18

custom parts:
  Teensy 4.1: The Teensy is a complete USB-based microcontoller development system, in a very small footprint, capable of implementing many types of projects. All programming is done via the USB port. No special programmer is needed, only a standard micro-USB cable and a PC or Macintosh with a USB port.
  elegoo-2.8in-tft-display: 2.8 Inch TFT LCD Touch Screen with SD Card Socket. 240*320 pixels RGB. 4 chip white LED backlight.
